// Logisim project House alarm - Final network.circ as structural Verilog: 1 circuit, main circuit main
module main (
  input  Open_Close,
  input  in_2,
  input  Choose_window,
  input  in_4,
  input  Open_Close_2,
  input  Open_Close_3,
  input  Open_Close_4,
  input  Open_Close_5,
  input  Open_Close_6,
  input  Open_Close_7,
  input  Alarm_ON,
  input  Change_passcode
);

  wire _1_2_out, _1_3_out, _1_out, _2_2_out, _2_3_out, _2_out, _3_2_out, _3_3_out, _3_out, _4_2_out,
       _4_3_out, _4_out, _5_2_out, _5_3_out, _5_out, _6_2_out, _6_3_out, _6_out, _7_2_out, _7_3_out, _7_out,
       Alarm_OFF_q, and_1_out, and_2_out, and_3_out, and_4_out, and_5_out, and_6_out, and_7_out, and_8_out,
       and_9_out, and_10_out, and_11_out, and_12_out, and_13_out, and_14_out, and_15_out, and_16_out,
       and_17_out, Cancel_out, clock_1_out, Clock_2_out, Close_out, comparator_1_eq, comparator_2_eq,
       comparator_3_eq, Confirm_passcode_out, demultiplexer_1_out0, demultiplexer_1_out1,
       demultiplexer_1_out2, demultiplexer_1_out3, demultiplexer_1_out4, demultiplexer_1_out5,
       demultiplexer_1_out6, demultiplexer_1_out7, nor_1_out, nor_2_out, nor_3_out, not_1_out, not_2_out,
       not_3_out, not_4_out, not_5_out, not_6_out, not_7_out, not_8_out, not_9_out, not_10_out, not_11_out,
       not_12_out, not_13_out, not_14_out, not_15_out, not_16_out, not_17_out, not_18_out, not_19_out,
       or_1_out, or_2_out, or_3_out, or_4_out, or_5_out, or_6_out, or_7_out, or_8_out, Reset_out,
       Reset_passcode_out, t_ff_1_qn, t_ff_2_qn, t_ff_3_qn, t_ff_4_qn, t_ff_5_qn, t_ff_6_qn, t_ff_7_qn,
       t_ff_27_qn, t_ff_28_qn, t_ff_29_qn, t_ff_30_qn, t_ff_31_q, t_ff_31_qn, t_ff_32_q, t_ff_33_q,
       t_ff_33_qn, t_ff_34_q, t_ff_35_q, t_ff_35_qn, t_ff_36_q, t_ff_37_qn, t_ff_38_q, t_ff_38_qn, t_ff_39_q,
       t_ff_39_qn, t_ff_40_q, t_ff_40_qn, t_ff_41_qn, t_ff_42_q, t_ff_42_qn, t_ff_43_q, t_ff_43_qn,
       t_ff_44_q, t_ff_44_qn, t_ff_45_q, t_ff_45_qn, xnor_1_out, xnor_2_out, xnor_3_out, xnor_4_out,
       xnor_5_out, xnor_6_out, xnor_7_out, xor_1_out, xor_2_out, xor_3_out, xor_4_out;
  wire [2:0] priority_encoder_1_out, priority_encoder_2_out, priority_encoder_3_out, t_ff_14_q, t_ff_15_q,
       t_ff_16_q, t_ff_23_q, t_ff_24_q, t_ff_25_q;

  Button Close (.out(Close_out));
  Demultiplexer #(.select(3), .enable("false")) demultiplexer_1 (
    .out0(demultiplexer_1_out0), .out1(demultiplexer_1_out1), .out2(demultiplexer_1_out2),
    .out3(demultiplexer_1_out3), .out4(demultiplexer_1_out4), .out5(demultiplexer_1_out5),
    .out6(demultiplexer_1_out6), .out7(demultiplexer_1_out7), .in(Close_out),
    .sel({in_2, Choose_window, in_4}));
  not not_1 (not_1_out, demultiplexer_1_out0);
  not not_2 (not_2_out, demultiplexer_1_out1);
  or or_1 (or_1_out, demultiplexer_1_out2, demultiplexer_1_out7);
  not not_3 (not_3_out, demultiplexer_1_out2);
  not not_4 (not_4_out, demultiplexer_1_out7);
  or or_2 (or_2_out, demultiplexer_1_out3, demultiplexer_1_out7);
  not not_5 (not_5_out, demultiplexer_1_out3);
  not not_6 (not_6_out, demultiplexer_1_out7);
  or or_3 (or_3_out, demultiplexer_1_out4, demultiplexer_1_out7);
  not not_7 (not_7_out, demultiplexer_1_out4);
  not not_8 (not_8_out, demultiplexer_1_out7);
  or or_4 (or_4_out, demultiplexer_1_out5, demultiplexer_1_out7);
  not not_9 (not_9_out, demultiplexer_1_out5);
  not not_10 (not_10_out, demultiplexer_1_out7);
  or or_5 (or_5_out, demultiplexer_1_out6, demultiplexer_1_out7);
  not not_11 (not_11_out, demultiplexer_1_out6);
  not not_12 (not_12_out, demultiplexer_1_out7);
  and and_1 (and_1_out, xnor_1_out, not_1_out);
  and and_2 (and_2_out, xnor_2_out, not_2_out);
  and and_3 (and_3_out, xnor_3_out, not_3_out, not_4_out);
  and and_4 (and_4_out, xnor_4_out, not_5_out, not_6_out);
  and and_5 (and_5_out, xnor_5_out, not_7_out, not_8_out);
  and and_6 (and_6_out, xnor_6_out, not_9_out, not_10_out);
  and and_7 (and_7_out, xnor_7_out, not_11_out, not_12_out);
  T_Flip_Flop t_ff_1 (.clk(demultiplexer_1_out0), .T(and_1_out), .Qn(t_ff_1_qn));  // open: Q, preset, reset, en
  T_Flip_Flop t_ff_2 (.clk(demultiplexer_1_out1), .T(and_2_out), .Qn(t_ff_2_qn));  // open: Q, preset, reset, en
  T_Flip_Flop t_ff_3 (.clk(or_1_out), .T(and_3_out), .Qn(t_ff_3_qn));  // open: Q, preset, reset, en
  T_Flip_Flop t_ff_4 (.clk(or_2_out), .T(and_4_out), .Qn(t_ff_4_qn));  // open: Q, preset, reset, en
  T_Flip_Flop t_ff_5 (.clk(or_3_out), .T(and_5_out), .Qn(t_ff_5_qn));  // open: Q, preset, reset, en
  T_Flip_Flop t_ff_6 (.clk(or_4_out), .T(and_6_out), .Qn(t_ff_6_qn));  // open: Q, preset, reset, en
  T_Flip_Flop t_ff_7 (.clk(or_5_out), .T(and_7_out), .Qn(t_ff_7_qn));  // open: Q, preset, reset, en
  xnor xnor_1 (xnor_1_out, Open_Close, t_ff_1_qn);
  LED Door_1 (.in(and_1_out));
  xnor xnor_2 (xnor_2_out, Open_Close_2, t_ff_2_qn);
  LED Door_2 (.in(and_2_out));
  xnor xnor_3 (xnor_3_out, Open_Close_3, t_ff_3_qn);
  LED Window_1 (.in(and_3_out));
  xnor xnor_4 (xnor_4_out, Open_Close_4, t_ff_4_qn);
  LED Window_2 (.in(and_4_out));
  xnor xnor_5 (xnor_5_out, Open_Close_5, t_ff_5_qn);
  LED Window_3 (.in(and_5_out));
  xnor xnor_6 (xnor_6_out, Open_Close_6, t_ff_6_qn);
  LED Window_4 (.in(and_6_out));
  xnor xnor_7 (xnor_7_out, Open_Close_7, t_ff_7_qn);
  LED Window_5 (.in(and_7_out));
  or or_6 (or_6_out, and_1_out, and_2_out);
  or or_7 (or_7_out, and_3_out, and_4_out, and_5_out, and_6_out, and_7_out);
  Button _1 (.out(_1_out));
  Button _2 (.out(_2_out));
  Button _3 (.out(_3_out));
  Button _4 (.out(_4_out));
  Button _5 (.out(_5_out));
  Button _6 (.out(_6_out));
  Button _7 (.out(_7_out));
  Button _1_2 (.out(_1_2_out));
  Button _2_2 (.out(_2_2_out));
  Button _3_2 (.out(_3_2_out));
  Button _4_2 (.out(_4_2_out));
  Button _5_2 (.out(_5_2_out));
  Button _6_2 (.out(_6_2_out));
  Button _7_2 (.out(_7_2_out));
  Button _1_3 (.out(_1_3_out));
  Button _2_3 (.out(_2_3_out));
  Button _3_3 (.out(_3_3_out));
  Button _4_3 (.out(_4_3_out));
  Button _5_3 (.out(_5_3_out));
  Button _6_3 (.out(_6_3_out));
  Button _7_3 (.out(_7_3_out));
  Button Cancel (.out(Cancel_out));
  Priority_Encoder priority_encoder_1 (
    .in0(1'b1), .in1(_1_out), .in2(_2_out), .in3(_3_out), .in4(_4_out), .in5(_5_out), .in6(_6_out),
    .in7(_7_out), .out(priority_encoder_1_out));  // open: en_in, gs, en_out
  Priority_Encoder priority_encoder_2 (
    .in0(1'b1), .in1(_1_2_out), .in2(_2_2_out), .in3(_3_2_out), .in4(_4_2_out), .in5(_5_2_out),
    .in6(_6_2_out), .in7(_7_2_out), .out(priority_encoder_2_out));  // open: en_in, gs, en_out
  Priority_Encoder priority_encoder_3 (
    .in0(1'b1), .in1(_1_3_out), .in2(_2_3_out), .in3(_3_3_out), .in4(_4_3_out), .in5(_5_3_out),
    .in6(_6_3_out), .in7(_7_3_out), .out(priority_encoder_3_out));  // open: en_in, gs, en_out
  T_Flip_Flop t_ff_8 (
    .clk(priority_encoder_1_out[2]), .T(priority_encoder_1_out[2]), .Q(t_ff_14_q[2]), .reset(Cancel_out));  // open: Qn, preset, en
  T_Flip_Flop t_ff_9 (
    .clk(priority_encoder_2_out[2]), .T(priority_encoder_2_out[2]), .Q(t_ff_15_q[2]), .reset(Cancel_out));  // open: Qn, preset, en
  T_Flip_Flop t_ff_10 (
    .clk(priority_encoder_3_out[2]), .T(priority_encoder_3_out[2]), .Q(t_ff_16_q[2]), .reset(Cancel_out));  // open: Qn, preset, en
  T_Flip_Flop t_ff_11 (
    .clk(priority_encoder_1_out[1]), .T(priority_encoder_1_out[1]), .Q(t_ff_14_q[1]), .reset(Cancel_out));  // open: Qn, preset, en
  T_Flip_Flop t_ff_12 (
    .clk(priority_encoder_2_out[1]), .T(priority_encoder_2_out[1]), .Q(t_ff_15_q[1]), .reset(Cancel_out));  // open: Qn, preset, en
  T_Flip_Flop t_ff_13 (
    .clk(priority_encoder_3_out[1]), .T(priority_encoder_3_out[1]), .Q(t_ff_16_q[1]), .reset(Cancel_out));  // open: Qn, preset, en
  nor nor_1 (nor_1_out, or_7_out, not_14_out);
  T_Flip_Flop t_ff_14 (
    .clk(priority_encoder_1_out[0]), .T(priority_encoder_1_out[0]), .Q(t_ff_14_q[0]), .reset(Cancel_out));  // open: Qn, preset, en
  T_Flip_Flop t_ff_15 (
    .clk(priority_encoder_2_out[0]), .T(priority_encoder_2_out[0]), .Q(t_ff_15_q[0]), .reset(Cancel_out));  // open: Qn, preset, en
  T_Flip_Flop t_ff_16 (
    .clk(priority_encoder_3_out[0]), .T(priority_encoder_3_out[0]), .Q(t_ff_16_q[0]), .reset(Cancel_out));  // open: Qn, preset, en
  LED Alarm_status (.in(nor_2_out));
  nor nor_2 (nor_2_out, or_6_out, not_13_out);
  not not_13 (not_13_out, t_ff_32_q);
  not not_14 (not_14_out, xor_1_out);
  xor xor_1 (xor_1_out, nor_3_out, t_ff_36_q);
  not not_15 (not_15_out, nor_1_out);
  not not_16 (not_16_out, xor_1_out);
  T_Flip_Flop t_ff_17 (
    .clk(t_ff_14_q[2]), .T(Change_passcode), .Q(t_ff_23_q[2]), .reset(Reset_passcode_out));  // open: Qn, preset, en
  T_Flip_Flop t_ff_18 (
    .clk(t_ff_15_q[2]), .T(Change_passcode), .Q(t_ff_24_q[2]), .reset(Reset_passcode_out));  // open: Qn, preset, en
  T_Flip_Flop t_ff_19 (
    .clk(t_ff_16_q[2]), .T(Change_passcode), .Q(t_ff_25_q[2]), .reset(Reset_passcode_out));  // open: Qn, preset, en
  LED Standby (.in(xor_2_out));
  xor xor_2 (xor_2_out, and_8_out, t_ff_34_q);
  and and_8 (and_8_out, or_6_out, t_ff_32_q);
  and and_9 (and_9_out, t_ff_32_q, or_7_out);
  and and_10 (and_10_out, and_11_out, nor_3_out, not_17_out);
  and and_11 (and_11_out, or_7_out, not_15_out);
  T_Flip_Flop t_ff_20 (
    .clk(t_ff_14_q[1]), .T(Change_passcode), .Q(t_ff_23_q[1]), .reset(Reset_passcode_out));  // open: Qn, preset, en
  T_Flip_Flop t_ff_21 (
    .clk(t_ff_15_q[1]), .T(Change_passcode), .Q(t_ff_24_q[1]), .reset(Reset_passcode_out));  // open: Qn, preset, en
  T_Flip_Flop t_ff_22 (
    .clk(t_ff_16_q[1]), .T(Change_passcode), .Q(t_ff_25_q[1]), .reset(Reset_passcode_out));  // open: Qn, preset, en
  not not_17 (not_17_out, t_ff_36_q);
  not not_18 (not_18_out, nor_3_out);
  T_Flip_Flop t_ff_23 (
    .clk(t_ff_14_q[0]), .T(Change_passcode), .Q(t_ff_23_q[0]), .reset(Reset_passcode_out));  // open: Qn, preset, en
  T_Flip_Flop t_ff_24 (
    .clk(t_ff_15_q[0]), .T(Change_passcode), .Q(t_ff_24_q[0]), .reset(Reset_passcode_out));  // open: Qn, preset, en
  T_Flip_Flop t_ff_25 (
    .clk(t_ff_16_q[0]), .T(Change_passcode), .Q(t_ff_25_q[0]), .reset(Reset_passcode_out));  // open: Qn, preset, en
  Button Reset_passcode (.out(Reset_passcode_out));
  or or_8 (or_8_out, t_ff_34_q, and_9_out, and_10_out);
  Comparator #(.width(3)) comparator_1 (.a(t_ff_14_q), .b(t_ff_23_q), .eq(comparator_1_eq));  // open: gt, lt
  Comparator #(.width(3)) comparator_2 (.a(t_ff_15_q), .b(t_ff_24_q), .eq(comparator_2_eq));  // open: gt, lt
  Comparator #(.width(3)) comparator_3 (.a(t_ff_16_q), .b(t_ff_25_q), .eq(comparator_3_eq));  // open: gt, lt
  and and_12 (and_12_out, comparator_1_eq, comparator_2_eq, comparator_3_eq);
  Button Confirm_passcode (.out(Confirm_passcode_out));
  and and_13 (and_13_out, and_12_out, Confirm_passcode_out);
  nor nor_3 (nor_3_out, Alarm_OFF_q, not_19_out);
  T_Flip_Flop Alarm_OFF (
    .clk(and_13_out), .T(and_13_out), .Q(Alarm_OFF_q), .reset(not_19_out));  // open: Qn, preset, en
  not not_19 (not_19_out, Alarm_ON);
  T_Flip_Flop t_ff_26 (.clk(t_ff_30_qn), .T(1'b1), .reset(Reset_out));  // open: Q, Qn, preset, en
  xor xor_3 (xor_3_out, nor_1_out, t_ff_32_q);
  T_Flip_Flop t_ff_27 (.clk(t_ff_31_q), .T(xor_3_out), .Qn(t_ff_27_qn), .reset(not_16_out));  // open: Q, preset, en
  xor xor_4 (xor_4_out, and_8_out, t_ff_34_q);
  T_Flip_Flop t_ff_28 (.clk(t_ff_33_q), .T(xor_4_out), .Qn(t_ff_28_qn), .reset(not_16_out));  // open: Q, preset, en
  T_Flip_Flop t_ff_29 (.clk(t_ff_35_q), .T(or_8_out), .Qn(t_ff_29_qn), .reset(not_18_out));  // open: Q, preset, en
  LED Siren (.in(and_14_out));
  and and_14 (and_14_out, or_8_out, clock_1_out);
  Clock clock_1 (.out(clock_1_out));
  T_Flip_Flop t_ff_30 (.clk(t_ff_37_qn), .T(1'b1), .Qn(t_ff_30_qn), .reset(Reset_out));  // open: Q, preset, en
  Button Reset (.out(Reset_out));
  T_Flip_Flop t_ff_31 (
    .clk(t_ff_38_q), .T(xor_3_out), .Q(t_ff_31_q), .Qn(t_ff_31_qn), .reset(not_16_out));  // open: preset, en
  T_Flip_Flop t_ff_32 (.clk(and_15_out), .T(1'b1), .Q(t_ff_32_q), .reset(not_16_out));  // open: Qn, preset, en
  and and_15 (and_15_out, t_ff_27_qn, t_ff_31_qn, t_ff_38_qn, t_ff_42_qn);
  T_Flip_Flop t_ff_33 (
    .clk(t_ff_39_q), .T(xor_4_out), .Q(t_ff_33_q), .Qn(t_ff_33_qn), .reset(not_16_out));  // open: preset, en
  T_Flip_Flop t_ff_34 (.clk(and_16_out), .T(1'b1), .Q(t_ff_34_q), .reset(not_16_out));  // open: Qn, preset, en
  and and_16 (and_16_out, t_ff_28_qn, t_ff_33_qn, t_ff_39_qn, t_ff_43_qn);
  T_Flip_Flop t_ff_35 (
    .clk(t_ff_40_q), .T(or_8_out), .Q(t_ff_35_q), .Qn(t_ff_35_qn), .reset(not_18_out));  // open: preset, en
  T_Flip_Flop t_ff_36 (.clk(and_17_out), .T(1'b1), .Q(t_ff_36_q), .reset(not_18_out));  // open: Qn, preset, en
  T_Flip_Flop t_ff_37 (.clk(t_ff_41_qn), .T(1'b1), .Qn(t_ff_37_qn), .reset(Reset_out));  // open: Q, preset, en
  T_Flip_Flop t_ff_38 (
    .clk(t_ff_42_q), .T(xor_3_out), .Q(t_ff_38_q), .Qn(t_ff_38_qn), .reset(not_16_out));  // open: preset, en
  T_Flip_Flop t_ff_39 (
    .clk(t_ff_43_q), .T(xor_4_out), .Q(t_ff_39_q), .Qn(t_ff_39_qn), .reset(not_16_out));  // open: preset, en
  T_Flip_Flop t_ff_40 (
    .clk(t_ff_44_q), .T(or_8_out), .Q(t_ff_40_q), .Qn(t_ff_40_qn), .reset(not_18_out));  // open: preset, en
  and and_17 (and_17_out, t_ff_29_qn, t_ff_35_qn, t_ff_40_qn, t_ff_44_qn, t_ff_45_qn);
  T_Flip_Flop t_ff_41 (.clk(or_8_out), .T(1'b1), .Qn(t_ff_41_qn), .reset(Reset_out));  // open: Q, preset, en
  T_Flip_Flop t_ff_42 (
    .clk(Clock_2_out), .T(xor_3_out), .Q(t_ff_42_q), .Qn(t_ff_42_qn), .reset(not_16_out));  // open: preset, en
  T_Flip_Flop t_ff_43 (
    .clk(Clock_2_out), .T(xor_4_out), .Q(t_ff_43_q), .Qn(t_ff_43_qn), .reset(not_16_out));  // open: preset, en
  T_Flip_Flop t_ff_44 (
    .clk(t_ff_45_q), .T(or_8_out), .Q(t_ff_44_q), .Qn(t_ff_44_qn), .reset(not_18_out));  // open: preset, en
  T_Flip_Flop t_ff_45 (
    .clk(Clock_2_out), .T(or_8_out), .Q(t_ff_45_q), .Qn(t_ff_45_qn), .reset(not_18_out));  // open: preset, en
  Clock Clock_2 (.out(Clock_2_out));

  // Notes on the sheet:
  //   Home automation
  //   Time to insert the code
  //   General register
  //   Time for the owner to leave
  //   Time before the siren stops
endmodule
